# Fritzing sketch BrewFocuserWiring (saved by Fritzing 0.9.3b)

parts:
  Part1 = MCP9808 High Accuracy I2C Temperature Sensor [part_number=1782]
  Part2 = Arduino Uno (Rev3)
  Part3 = Arduino Prototyping Shield
  J2 = female pin header, 8 pins [form="♀ (female)"]
  J3 = female pin header, 8 pins [form="♀ (female)"]
  J4 = female pin header, 6 pins [form="♀ (female)"]
  J1 = female pin header, 10 pins [form="♀ (female)"]
  M1 = Stepper Motor - Bipolar
  J5 = Screw terminal - 2 pins [package=THT]
  Motor = DB9 Connector [package=db9]
  MotorConx = DB9 Connector [package=db9]
  J6 = screw terminal, 4 pins
  S5 = Round Pushbutton
  TempComp_LED3 = LED - 3mm [color="Yellow (595nm)" package="3 mm [THT]"]
  S6_In = Round Pushbutton
  C1 = Electrolytic Capacitor [capacitance=1µF package="100 mil [THT, electrolytic]"]
  S7 = Toggle Switch [package=THT]
  J8 = male pin header, 5 pins [form="♂ (male)"]
  LEDIn = LED - 3mm [color="Green (555nm)" package="3 mm [THT]"]
  LEDOut = LED - 3mm [color="Red (633nm)" package="3 mm [THT]"]
  R2 = Resistor [tolerance=±5% resistance=1k package=THT]
  MotorB = DB9 Connector [package=db9]
  MotorA = DB9 Connector [package=db9]
  J9 = male pin header, 4 pins [form="♂ (male)"]
  TempConx = DB9 Connector [package=db9]
  TempA = DB9 Connector [package=db9]
  J7 = screw terminal, 5 pins

nets:
  N1: Part1.VDD, J9.pin1, TempA.5
  N2: Part1.GND, TempA.7
  N3: Part1.SCL, J9.pin3, TempA.6
  N4: Part1.SDA, J9.pin4, TempA.8
  N5: Part2.GND, Part3.D12, J1.pin6
  N6: Part3.A0, J4.pin1
  N7: Part3.A1, J4.pin2
  N8: Part3.A2, J4.pin3
  N9: Part3.A3, J4.pin4
  N10: Part3.A4, J4.pin5
  N11: Part3.A5, J4.pin6
  N12: Part3.D0(RX), J2.pin8
  N13: Part3.D1(TX), J2.pin7
  N14: Part3.D2, J2.pin6
  N15: Part3.D3, J2.pin5
  N16: Part3.D4, J2.pin4, S5.leg0
  N17: Part3.D5, J2.pin3, S6_In.leg0
  N18: Part3.D6, Part3.N$240, J2.pin2
  N19: Part3.D7, Part3.N$156, J2.pin1
  N20: Part3.IOREF, J3.pin1, J3.pin2
  N21: Part3.RESET, J3.pin3, S7.L2, J8.pin1
  N22: Part3.3.3V, J3.pin4, J8.pin2
  N23: Part3.+5V, J3.pin5, J5.pin1, J8.pin3, TempConx.9
  N24: Part3.GND, J3.pin6, J3.pin7, J1.pin4, J5.pin2, S5.leg1, S6_In.leg1, C1.-, J8.pin4, J8.pin5, TempConx.7
  N25: Part3.+9V, J3.pin8
  N26: Part3.D8, J1.pin10
  N27: Part3.D9, J1.pin9
  N28: Part3.D10, J1.pin8
  N29: Part3.D11, J1.pin7
  N30: Part3.D13, J1.pin5
  N31: Part3.AREF, J1.pin3, R2.Pin_1
  N32: Part3.SDA, J1.pin2, TempConx.6
  N33: Part3.SCL, J1.pin1, TempConx.8
  N34: Part3.N$64, LEDIn.cathode
  N35: Part3.N$135, Part3.N$239, Part3.N$251, Part3.N$411, TempComp_LED3.cathode, LEDIn.anode, LEDOut.cathode, R2.Pin_0
  N36: Part3.N$268, LEDOut.anode
  N37: Part3.N$321, J6.pin1
  N38: Part3.N$322, J6.pin2
  N39: Part3.N$324, J6.pin3
  N40: Part3.N$325, J6.pin4
  N41: M1.A, Motor.9
  N42: M1.C, Motor.8
  N43: M1.B, Motor.6, Motor.7
  N44: M1.D, Motor.5
  N45: MotorConx.5, J7.pin4
  N46: MotorConx.6, J7.pin5
  N47: MotorConx.7, J7.pin1
  N48: MotorConx.8, MotorConx.9, J7.pin2, J7.pin3
  N49: C1.+, S7.COM
  N50: MotorB.5, MotorA.9
  N51: MotorB.6, MotorA.8
  N52: MotorB.7, MotorA.7
  N53: MotorB.8, MotorA.6
  N54: MotorB.9, MotorA.5

notes:
  Expanded Temperature jumper
  In
  Out
  Run/Load
  Motor Cable
  Temperature Cable

custom parts:
  MCP9808 High Accuracy I2C Temperature Sensor: This I2C digital temperature sensor is one of the more accurate/precise we've ever seen, with a typical accuracy of ±0.25°C over the sensor's -40°C to +125°C range and precision of +0.0625°C. They work great with any microcontroller using standard i2c. There are 3 address pins so you can connect up to 8 to a single I2C bus without address collisions. Best of all, a wide voltage range makes is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
